// Logisim project more_advance.circ as structural Verilog: 3 circuits, main circuit four_bit_computer
// reset
module four_bit_computer (
);

  wire and_1_out, and_2_out, and_3_out, and_4_out, and_5_out, and_6_out, and_7_out, and_8_out,
       bit_extender_1_out, d_ff_1_q, d_ff_2_q, d_ff_3_q, d_ff_4_q, d_ff_5_q, demultiplexer_1_out5,
       demultiplexer_1_out6, demultiplexer_1_out7, GlobalClock_out, GlobalReset_out, nor_1_out, nor_2_out,
       or_1_out, or_2_out, or_3_out, or_4_out, PC_carry;
  wire [0:0] demultiplexer_1_out2;
  wire [1:0] demultiplexer_1_out4;
  wire [2:0] bcd_to_7_segment_decoder_1_p1, bcd_to_7_segment_decoder_2_p1, bcd_to_7_segment_decoder_3_p1,
       MainRom_data_2, multiplexer_1_out, multiplexer_2_out, multiplexer_3_out, undriven;
  wire [3:3] MainRom_data;
  wire [6:0] PC_q;

  Counter #(.max('h7f), .trigger("falling"), .width(7)) PC (
    .clr(or_1_out), .load(d_ff_4_q), .up(1'b1), .count(1'b1), .clk(GlobalClock_out),
    .D({4'b0000, MainRom_data_2}), .carry(PC_carry), .Q(PC_q));
  or or_1 (or_1_out, GlobalReset_out, GlobalReset_out);
  ROM #(.addrWidth(7), .dataWidth(4)) MainRom (.addr(PC_q), .data({MainRom_data[3], MainRom_data_2}));
  Clock #(.phaseOffset(1)) GlobalClock (.out(GlobalClock_out));
  Button GlobalReset (.out(GlobalReset_out));
  _7_Segment_Display u_7_segment_display_1 ();  // open: g, f, a, b, e, d, c, dp
  // BCD_to_7_Segment_decoder bcd_to_7_segment_decoder_1: pin names not known; wires that end beside it: {1'b0, bcd_to_7_segment_decoder_1_p1}
  _7_Segment_Display u_7_segment_display_2 ();  // open: g, f, a, b, e, d, c, dp
  // BCD_to_7_Segment_decoder bcd_to_7_segment_decoder_2: pin names not known; wires that end beside it: {1'b0, bcd_to_7_segment_decoder_2_p1}
  or or_2 (or_2_out, demultiplexer_1_out2[0], demultiplexer_1_out4[0], demultiplexer_1_out4[1], demultiplexer_1_out5, demultiplexer_1_out6, demultiplexer_1_out7);
  and and_1 (and_1_out, MainRom_data[3], or_2_out);
  _7_Segment_Display u_7_segment_display_3 ();  // open: g, f, a, b, e, d, c, dp
  // BCD_to_7_Segment_decoder bcd_to_7_segment_decoder_3: pin names not known; wires that end beside it: {1'b0, bcd_to_7_segment_decoder_3_p1}
  Demultiplexer #(.select(3)) demultiplexer_1 (
    .out2(demultiplexer_1_out2[0]), .out3(demultiplexer_1_out4[0]), .out4(demultiplexer_1_out4[1]),
    .out5(demultiplexer_1_out5), .out6(demultiplexer_1_out6), .out7(demultiplexer_1_out7),
    .in(MainRom_data[3]), .sel(MainRom_data_2));  // open: out0, out1
  and and_2 (and_2_out, demultiplexer_1_out2[0], nor_1_out);
  // Binary_to_BCD_converter #(.binvalue(4)) binary_to_bcd_converter_1: pin names not known; wires that end beside it: {1'b0, MainRom_data_2}, GlobalClock_out, demultiplexer_1_out5
  Multiplexer #(.select(2), .width(3)) multiplexer_1 (
    .in0(undriven), .in1(bcd_to_7_segment_decoder_2_p1), .in2(bcd_to_7_segment_decoder_3_p1),
    .out(multiplexer_1_out), .sel(demultiplexer_1_out4));  // open: in3
  D_Flip_Flop d_ff_1 (
    .D(and_2_out), .clk(GlobalClock_out), .Q(d_ff_1_q), .preset(and_2_out), .reset(GlobalReset_out));  // open: Qn
  Register #(.width(3)) A (
    .D(multiplexer_1_out), .en(and_3_out), .clk(GlobalClock_out), .Q(bcd_to_7_segment_decoder_1_p1),
    .clr(GlobalReset_out));
  and and_3 (and_3_out, d_ff_1_q, nor_2_out);
  and and_4 (and_4_out, demultiplexer_1_out4[0], nor_1_out);
  Bit_Extender #(.in_width(3), .out_width(1)) bit_extender_1 (
    .in(bcd_to_7_segment_decoder_3_p1), .out(bit_extender_1_out));
  and and_5 (and_5_out, demultiplexer_1_out6, bit_extender_1_out);
  or or_3 (or_3_out, demultiplexer_1_out7, and_5_out);
  D_Flip_Flop d_ff_2 (
    .D(or_3_out), .clk(GlobalClock_out), .Q(d_ff_2_q), .preset(or_3_out), .reset(or_4_out));  // open: Qn
  or or_4 (or_4_out, and_1_out, GlobalReset_out);
  D_Flip_Flop d_ff_3 (
    .D(and_4_out), .clk(GlobalClock_out), .Q(d_ff_3_q), .preset(and_4_out), .reset(GlobalReset_out));  // open: Qn
  D_Flip_Flop d_ff_4 (.D(d_ff_2_q), .clk(GlobalClock_out), .Q(d_ff_4_q));  // open: Qn, preset, reset
  LedBar #(.matrixcols(9)) MainOutput (
    .led0(bcd_to_7_segment_decoder_1_p1[2]), .led1(bcd_to_7_segment_decoder_1_p1[1]),
    .led2(bcd_to_7_segment_decoder_1_p1[0]), .led3(bcd_to_7_segment_decoder_2_p1[2]),
    .led4(bcd_to_7_segment_decoder_2_p1[1]), .led5(bcd_to_7_segment_decoder_2_p1[0]),
    .led6(bcd_to_7_segment_decoder_3_p1[2]), .led7(bcd_to_7_segment_decoder_3_p1[1]),
    .led8(bcd_to_7_segment_decoder_3_p1[0]));
  Multiplexer #(.select(2), .width(3)) multiplexer_2 (
    .in0(undriven), .in1(bcd_to_7_segment_decoder_1_p1), .in2(bcd_to_7_segment_decoder_3_p1),
    .out(multiplexer_2_out), .sel({demultiplexer_1_out4[1], demultiplexer_1_out2[0]}));  // open: in3
  and and_6 (and_6_out, d_ff_3_q, nor_2_out);
  nor nor_1 (nor_1_out, and_3_out, and_6_out, and_8_out);
  Register #(.width(3)) B (
    .D(multiplexer_2_out), .en(and_6_out), .clk(GlobalClock_out), .Q(bcd_to_7_segment_decoder_2_p1),
    .clr(GlobalReset_out));
  and and_7 (and_7_out, demultiplexer_1_out4[1], nor_1_out);
  nor nor_2 (nor_2_out, demultiplexer_1_out2[0], demultiplexer_1_out4[0], demultiplexer_1_out4[1]);
  D_Flip_Flop d_ff_5 (
    .D(and_7_out), .clk(GlobalClock_out), .Q(d_ff_5_q), .preset(and_7_out), .reset(GlobalReset_out));  // open: Qn
  Multiplexer #(.select(2), .width(3)) multiplexer_3 (
    .in0(undriven), .in1(bcd_to_7_segment_decoder_1_p1), .in2(bcd_to_7_segment_decoder_2_p1),
    .out(multiplexer_3_out), .sel({demultiplexer_1_out4[0], demultiplexer_1_out2[0]}));  // open: in3
  and and_8 (and_8_out, d_ff_5_q, nor_2_out);
  Register #(.width(3)) C (
    .D(multiplexer_3_out), .en(and_8_out), .clk(GlobalClock_out), .Q(bcd_to_7_segment_decoder_3_p1),
    .clr(GlobalReset_out));
  // also tied to GND on the sheet: PC_carry

  // Notes on the sheet:
  //   contents of MainRom (hex, n*v repeats v):
  //   a 3 c 0 a 6 c 1 e
endmodule

module Add_Sub (
  input  [2:0] old_value,
  input  [2:0] value,
  input  sel_add_sub,
  output [2:0] new_value
);

  wire subtractor_1_bout;
  wire [2:0] adder_1_out, subtractor_1_out;

  Adder #(.width(3)) adder_1 (.a(old_value), .b(value), .out(adder_1_out));  // open: cin, cout
  Subtractor #(.width(3)) subtractor_1 (
    .a(old_value), .b(value), .out(subtractor_1_out), .bout(subtractor_1_bout));  // open: bin
  Multiplexer #(.width(3)) multiplexer_1 (
    .in0(adder_1_out), .in1(subtractor_1_out), .out(new_value), .sel(sel_add_sub));
  // also tied to GND on the sheet: subtractor_1_bout
endmodule

module toggled_register (
  input  [2:0] DataIn,
  input  [2:0] RegX,
  input  [2:0] RegY,
  input  [1:0] select_in,
  input  toggle,
  input  is_write,
  input  writing,
  input  clock,
  input  Reset,
  output [2:0] DataOut
);

  wire d_ff_1_q;
  wire [2:0] multiplexer_1_out;

  D_Flip_Flop d_ff_1 (.D(toggle), .clk(clock), .Q(d_ff_1_q), .preset(toggle), .reset(Reset));  // open: Qn
  Multiplexer #(.select(2), .width(3)) multiplexer_1 (
    .in0(DataIn), .in1(RegX), .in2(RegY), .out(multiplexer_1_out), .sel(select_in));  // open: in3
  and and_1 (writing, d_ff_1_q, is_write);
  Register #(.width(3)) register_1 (.D(multiplexer_1_out), .en(writing), .clk(clock), .Q(DataOut), .clr(Reset));
endmodule
