// Logisim project more_advance_big_jump.circ as structural Verilog: 6 circuits, main circuit four_bit_computer
// reset
module four_bit_computer (
  input  [3:0] in_1,
  input  [1:0] in_2
);

  wire A_writing, and_1_out, and_2_out, and_3_out, and_4_out, and_5_out, B_writing, C_writing, clock,
       d_ff_1_q, d_ff_1_qn, d_ff_2_q, demultiplexer_1_out6, demultiplexer_1_out7, GlobalReset_out,
       is_writing, LE, nor_1_out, nor_2_out, not_1_out, or_1_out, or_3_out, or_4_out, or_5_out, PC_carry,
       reset, systemreset, three_bit_or_with_fourth_bit_and_out_3, undriven, undriven_2, undriven_3;
  wire [1:0] demultiplexer_1_out0, multiplexer_2_out, register_1_q, register_2_q;
  wire [2:0] selReg;
  wire [3:0] A_dataout, add_sub_1_new_value, B_dataout, C_dataout, data, multiplexer_1_out, temp_reg_q;
  wire [7:0] address_buffer_1_total_address, PC_q;

  Counter #(.trigger("falling")) PC (
    .clr(reset), .load(LE), .up(1'b1), .count(1'b1), .clk(clock), .D(address_buffer_1_total_address),
    .carry(PC_carry), .Q(PC_q));
  Multiplexer #(.select(3), .width(4)) multiplexer_1 (
    .in0(in_1), .in1(A_dataout), .in2(B_dataout), .in3(in_1), .in4(C_dataout), .in5(in_1), .in6(in_1),
    .in7(in_1), .out(multiplexer_1_out), .sel(selReg));
  ROM #(.dataWidth(4)) MainRom (.addr(PC_q), .data(data));
  Register #(.width(4)) temp_reg (.D(multiplexer_1_out), .en(or_1_out), .clk(clock), .Q(temp_reg_q), .clr(reset));
  or or_1 (or_1_out, selReg[2], selReg[1], selReg[0]);
  Clock #(.phaseOffset(1)) GlobalClock (.out(clock));
  address_buffer address_buffer_1 (
    .ab_reset(or_3_out), .ab_clock(clock), .addressoffset(data),
    .total_address(address_buffer_1_total_address));
  or or_2 (reset, systemreset, GlobalReset_out);
  Register #(.width(2)) register_1 (.D(multiplexer_2_out), .en(not_1_out), .clk(clock), .Q(register_1_q), .clr(reset));
  Button GlobalReset (.out(GlobalReset_out));
  or or_3 (or_3_out, or_4_out, reset);
  Register #(.width(2)) register_2 (.D(register_1_q), .en(not_1_out), .clk(clock), .Q(register_2_q), .clr(reset));
  Multiplexer #(.width(2)) multiplexer_2 (
    .in0(in_2), .in1(demultiplexer_1_out0), .out(multiplexer_2_out), .sel(not_1_out));
  not not_1 (not_1_out, is_writing);
  Hex_Digit_Display hex_digit_display_1 (.value(A_dataout));  // open: dp
  Add_Sub add_sub_1 (.old_value(temp_reg_q), .value(data), .sel_add_sub(register_2_q), .new_value(add_sub_1_new_value));
  Hex_Digit_Display hex_digit_display_2 (.value(B_dataout));  // open: dp
  Hex_Digit_Display hex_digit_display_3 (.value(C_dataout));  // open: dp
  Demultiplexer #(.select(3)) demultiplexer_1 (
    .out0(demultiplexer_1_out0[0]), .out1(demultiplexer_1_out0[1]), .out2(selReg[0]), .out3(selReg[1]),
    .out4(selReg[2]), .out5(systemreset), .out6(demultiplexer_1_out6), .out7(demultiplexer_1_out7),
    .in(data[3]), .sel(data[2:0]));
  and and_1 (and_1_out, selReg[0], nor_1_out);
  and and_2 (and_2_out, demultiplexer_1_out7, ~is_writing);  // AND_Gate
  and and_3 (and_3_out, ~is_writing, demultiplexer_1_out6);  // AND_Gate
  D_Flip_Flop d_ff_1 (.D(undriven), .clk(clock), .Q(d_ff_1_q), .Qn(d_ff_1_qn), .preset(undriven));  // open: reset
  and_3_1 three_bit_or_with_fourth_bit_and (
    .one_bit(and_3_out), .three_bit_bus(C_dataout), .out_3(three_bit_or_with_fourth_bit_and_out_3));
  or or_4 (or_4_out, and_2_out, three_bit_or_with_fourth_bit_and_out_3);
  Shift_Register #(.length(3)) shift_register_1 (
    .shift(clock), .in(or_4_out), .clk(clock), .out(LE), .clr(or_5_out));  // open: load, d0, q0, d1, q1, d2, q2
  buf or_5 (or_5_out, reset);  // OR_Gate
  D_Flip_Flop d_ff_2 (.D(d_ff_1_q), .clk(d_ff_1_qn), .Q(d_ff_2_q), .preset(d_ff_1_q));  // open: Qn, reset
  toggled_register A (
    .DataIn(add_sub_1_new_value), .RegX(B_dataout), .RegY(C_dataout), .select_in(selReg[2:1]),
    .toggle(and_1_out), .is_write(nor_2_out), .clock(clock), .Reset(reset), .writing(A_writing),
    .DataOut(A_dataout));
  and and_4 (and_4_out, selReg[1], nor_1_out);
  LedBar #(.matrixcols(12)) MainOutput (
    .led0(A_dataout[3]), .led1(A_dataout[2]), .led2(A_dataout[1]), .led3(A_dataout[0]), .led4(B_dataout[3]),
    .led5(B_dataout[2]), .led6(B_dataout[1]), .led7(B_dataout[0]), .led8(C_dataout[3]), .led9(C_dataout[2]),
    .led10(C_dataout[1]), .led11(C_dataout[0]));
  nor nor_1 (nor_1_out, A_writing, B_writing, C_writing);
  D_Flip_Flop d_ff_3 (.D(d_ff_2_q), .clk(clock), .preset(undriven_2), .reset(undriven_3));  // open: Q, Qn
  or or_6 (is_writing, A_writing, B_writing, C_writing);
  nor nor_2 (nor_2_out, selReg[0], selReg[1], selReg[2]);
  and and_5 (and_5_out, selReg[2], nor_1_out);
  toggled_register B (
    .DataIn(add_sub_1_new_value), .RegX(A_dataout), .RegY(C_dataout), .select_in({selReg[2], selReg[0]}),
    .toggle(and_4_out), .is_write(nor_2_out), .clock(clock), .Reset(reset), .writing(B_writing),
    .DataOut(B_dataout));
  toggled_register C (
    .DataIn(add_sub_1_new_value), .RegX(A_dataout), .RegY(B_dataout), .select_in(selReg[1:0]),
    .toggle(and_5_out), .is_write(nor_2_out), .clock(clock), .Reset(reset), .writing(C_writing),
    .DataOut(C_dataout));
  // also tied to GND on the sheet: PC_carry

  // Notes on the sheet:
  //   contents of MainRom (hex, n*v repeats v):
  //   a 9 b 9 c 9 9 c 1 e 0 6 0 d
endmodule

module Add_Sub (
  input  [3:0] old_value,
  input  [3:0] value,
  input  [1:0] sel_add_sub,
  output [3:0] new_value
);

  wire subtractor_1_bout;
  wire [3:0] adder_1_out, subtractor_1_out;

  Adder #(.width(4)) adder_1 (.a(old_value), .b(value), .out(adder_1_out));  // open: cin, cout
  Subtractor #(.width(4)) subtractor_1 (
    .a(old_value), .b(value), .out(subtractor_1_out), .bout(subtractor_1_bout));  // open: bin
  Multiplexer #(.select(2), .width(4)) multiplexer_1 (
    .in0(value), .in1(adder_1_out), .in2(subtractor_1_out), .in3(value), .out(new_value), .sel(sel_add_sub));
  // also tied to GND on the sheet: subtractor_1_bout
endmodule

module toggled_register (
  input  [3:0] DataIn,
  input  [3:0] RegX,
  input  [3:0] RegY,
  input  [1:0] select_in,
  input  toggle,
  input  is_write,
  input  clock,
  input  Reset,
  output writing,
  output [3:0] DataOut
);

  wire d_ff_1_q;
  wire [3:0] multiplexer_1_out;

  D_Flip_Flop d_ff_1 (.D(toggle), .clk(clock), .Q(d_ff_1_q), .preset(toggle), .reset(Reset));  // open: Qn
  Multiplexer #(.select(2), .width(4)) multiplexer_1 (
    .in0(DataIn), .in1(RegX), .in2(RegY), .out(multiplexer_1_out), .sel(select_in));  // open: in3
  and and_1 (writing, d_ff_1_q, is_write);
  Register #(.width(4)) register_1 (.D(multiplexer_1_out), .en(writing), .clk(clock), .Q(DataOut), .clr(Reset));
endmodule

module and_3_1 (
  input  [3:0] three_bit_bus,
  input  one_bit,
  output out_3
);

  wire or_1_out;

  or or_1 (or_1_out, three_bit_bus[0], three_bit_bus[1], three_bit_bus[2], three_bit_bus[3]);
  and and_1 (out_3, or_1_out, one_bit);
endmodule

module advance_splitter (
  input  [1:0] two,
  input  [2:0] three,
  input  [3:0] four,
  input  [4:0] five,
  input  [5:0] six,
  input  [6:0] seven,
  input  [7:0] eight,
  output [1:0] Otwo,
  output [2:0] Othree,
  output [3:0] Ofour,
  output [4:0] oFive,
  output [5:0] oSix,
  output [6:0] oSeven,
  output [7:0] oEight
);


  assign five = eight[4:0];
  assign four = eight[3:0];
  assign oEight = eight;
  assign oFive = eight[4:0];
  assign Ofour = eight[3:0];
  assign oSeven = eight[6:0];
  assign oSix = eight[5:0];
  assign Othree = eight[2:0];
  assign Otwo = eight[1:0];
  assign seven = eight[6:0];
  assign six = eight[5:0];
  assign three = eight[2:0];
  assign two = eight[1:0];
endmodule

module address_buffer (
  input  ab_reset,
  input  ab_clock,
  input  [3:0] addressoffset,
  output [7:0] total_address
);

  // Shift_Register #(.width(4)) shift_register_1: pin names not known; wires that end beside it: ab_reset, ab_clock, ab_clock, addressoffset, total_address[3:0], total_address[7:4]
endmodule
