// Logisim project single_bit_comp.circ as structural Verilog: 1 circuit, main circuit four_bit_computer
// reset
module four_bit_computer (
);

  wire d_ff_1_q, d_ff_2_q, d_ff_3_q, d_ff_4_q, demultiplexer_1_out0, demultiplexer_1_out1,
       demultiplexer_1_out2, demultiplexer_1_out3, demultiplexer_1_out4, demultiplexer_1_out5,
       demultiplexer_1_out6, demultiplexer_1_out7, demultiplexer_2_out1, GlobalClock_out, GlobalReset_out,
       not_1_out, or_3_out, or_5_out, or_6_out;
  wire [1:0] A_q, B_q, C_q, or_1_out, or_2_out, or_4_out;
  wire [3:0] counter_1_q;
  wire [3:1] MainRom_data;
  wire [3:3] MainRom_data_2;

  Counter #(.max('hf), .width(4)) counter_1 (
    .clr(GlobalReset_out), .load(d_ff_3_q), .up(1'b1), .count(1'b1), .clk(GlobalClock_out),
    .D({MainRom_data, 1'b0}), .Q(counter_1_q));  // open: carry
  ROM #(.addrWidth(4), .dataWidth(4)) MainRom (.addr(counter_1_q), .data({MainRom_data_2[3], MainRom_data}));
  Clock GlobalClock (.out(GlobalClock_out));
  Button GlobalReset (.out(GlobalReset_out));
  not not_1 (not_1_out, MainRom_data_2[3]);
  Demultiplexer #(.select(3)) demultiplexer_1 (
    .out0(demultiplexer_1_out0), .out1(demultiplexer_1_out1), .out2(demultiplexer_1_out2),
    .out3(demultiplexer_1_out3), .out4(demultiplexer_1_out4), .out5(demultiplexer_1_out5),
    .out6(demultiplexer_1_out6), .out7(demultiplexer_1_out7), .in(MainRom_data_2[3]), .sel(MainRom_data));
  Demultiplexer #(.select(3)) demultiplexer_2 (
    .out1(demultiplexer_2_out1), .in(not_1_out), .sel(MainRom_data));  // open: out0, out2, out3, out4, out5, out6, out7
  or or_1 (or_1_out[0], 1'b0, demultiplexer_2_out1);
  or or_2 (or_2_out[0], 1'b0, demultiplexer_2_out1);
  D_Flip_Flop d_ff_1 (
    .D(or_3_out), .clk(GlobalClock_out), .Q(d_ff_1_q), .preset(or_3_out), .reset(MainRom_data_2[3]));  // open: Qn
  or or_3 (or_3_out, demultiplexer_1_out0, demultiplexer_1_out3, demultiplexer_1_out4, demultiplexer_1_out6);
  or or_4 (or_4_out[0], 1'b0, demultiplexer_2_out1);
  Register #(.width(2)) A (.D(or_1_out), .en(d_ff_1_q), .clk(GlobalClock_out), .Q(A_q), .clr(GlobalReset_out));
  or or_5 (or_5_out, demultiplexer_1_out1, demultiplexer_1_out3, demultiplexer_1_out5, demultiplexer_1_out6);
  D_Flip_Flop d_ff_2 (
    .D(or_5_out), .clk(GlobalClock_out), .Q(d_ff_2_q), .preset(or_5_out), .reset(MainRom_data_2[3]));  // open: Qn
  Register #(.width(2)) B (.D(or_2_out), .en(d_ff_2_q), .clk(GlobalClock_out), .Q(B_q), .clr(GlobalReset_out));
  D_Flip_Flop d_ff_3 (
    .D(demultiplexer_1_out7), .clk(GlobalClock_out), .Q(d_ff_3_q), .preset(demultiplexer_1_out7),
    .reset(MainRom_data_2[3]));  // open: Qn
  LedBar #(.matrixcols(6)) ledbar_1 (
    .led0(A_q[0]), .led1(A_q[0]), .led2(B_q[0]), .led3(B_q[0]), .led4(C_q[0]), .led5(C_q[0]));
  D_Flip_Flop d_ff_4 (
    .D(or_6_out), .clk(GlobalClock_out), .Q(d_ff_4_q), .preset(or_6_out), .reset(MainRom_data_2[3]));  // open: Qn
  or or_6 (or_6_out, demultiplexer_1_out2, demultiplexer_1_out4, demultiplexer_1_out5, demultiplexer_1_out6);
  Register #(.width(2)) C (.D(or_4_out), .en(d_ff_4_q), .clk(GlobalClock_out), .Q(C_q), .clr(GlobalReset_out));
  // Pins of 1 and 2 bits meet at or_1_out
  // Pins of 1 and 2 bits meet at or_2_out
  // Pins of 1 and 2 bits meet at or_4_out
  // Pins of 1 and 2 bits meet at A_q
  // Pins of 1 and 2 bits meet at B_q
  // Pins of 1 and 2 bits meet at C_q

  // Notes on the sheet:
  //   contents of MainRom (hex, n*v repeats v):
  //   0 0 8 1 9 1 a 1 8 0 9 0 a 0 f
endmodule
