// Logisim project three_bit_comp.circ as structural Verilog: 1 circuit, main circuit four_bit_computer
// reset
module four_bit_computer (
);

  wire d_ff_1_q, d_ff_2_q, d_ff_3_q, d_ff_4_q, demultiplexer_1_out0, demultiplexer_1_out1,
       demultiplexer_1_out2, demultiplexer_1_out3, demultiplexer_1_out4, demultiplexer_1_out5,
       demultiplexer_1_out6, demultiplexer_1_out7, GlobalClock_out, GlobalReset_out, not_1_out, or_1_out,
       or_2_out, or_3_out, or_4_out;
  wire [2:0] bcd_to_7_segment_decoder_1_p1, bcd_to_7_segment_decoder_2_p1, bcd_to_7_segment_decoder_3_p1,
       binary_to_bcd_converter_1_p4, MainRom_data_2;
  wire [3:3] binary_to_bcd_converter_1_p4_2, MainRom_data;
  wire [6:0] adder_1_out, counter_1_q;
  wire [7:0] demultiplexer_2_out0;

  Counter #(.max('h7f), .width(7)) counter_1 (
    .clr(GlobalReset_out), .load(d_ff_3_q), .up(1'b1), .count(1'b1), .clk(GlobalClock_out), .D(adder_1_out),
    .Q(counter_1_q));  // open: carry
  ROM #(.addrWidth(7), .dataWidth(4)) MainRom (.addr(counter_1_q), .data({MainRom_data[3], MainRom_data_2}));
  Adder #(.width(7)) adder_1 (.a({4'b0000, MainRom_data_2}), .b(7'b0000010), .out(adder_1_out));  // open: cin, cout
  Clock GlobalClock (.out(GlobalClock_out));
  Button GlobalReset (.out(GlobalReset_out));
  _7_Segment_Display u_7_segment_display_1 ();  // open: g, f, a, b, e, d, c, dp
  // BCD_to_7_Segment_decoder bcd_to_7_segment_decoder_1: pin names not known; wires that end beside it: {1'b0, bcd_to_7_segment_decoder_1_p1}
  _7_Segment_Display u_7_segment_display_2 ();  // open: g, f, a, b, e, d, c, dp
  // BCD_to_7_Segment_decoder bcd_to_7_segment_decoder_2: pin names not known; wires that end beside it: {1'b0, bcd_to_7_segment_decoder_2_p1}
  not not_1 (not_1_out, MainRom_data[3]);
  _7_Segment_Display u_7_segment_display_3 ();  // open: g, f, a, b, e, d, c, dp
  // BCD_to_7_Segment_decoder bcd_to_7_segment_decoder_3: pin names not known; wires that end beside it: {1'b0, bcd_to_7_segment_decoder_3_p1}
  Demultiplexer #(.select(3)) demultiplexer_1 (
    .out0(demultiplexer_1_out0), .out1(demultiplexer_1_out1), .out2(demultiplexer_1_out2),
    .out3(demultiplexer_1_out3), .out4(demultiplexer_1_out4), .out5(demultiplexer_1_out5),
    .out6(demultiplexer_1_out6), .out7(demultiplexer_1_out7), .in(MainRom_data[3]), .sel(MainRom_data_2));
  Demultiplexer #(.select(3)) demultiplexer_2 (
    .out0(demultiplexer_2_out0[0]), .out1(demultiplexer_2_out0[1]), .out2(demultiplexer_2_out0[2]),
    .out3(demultiplexer_2_out0[3]), .out4(demultiplexer_2_out0[4]), .out5(demultiplexer_2_out0[5]),
    .out6(demultiplexer_2_out0[6]), .out7(demultiplexer_2_out0[7]), .in(not_1_out), .sel(MainRom_data_2));
  // Binary_to_BCD_converter #(.binvalue(4)) binary_to_bcd_converter_1: pin names not known; wires that end beside it: MainRom_data_2, demultiplexer_2_out0, {1'b0, MainRom_data_2}, {binary_to_bcd_converter_1_p4_2[3], binary_to_bcd_converter_1_p4}
  D_Flip_Flop d_ff_1 (
    .D(or_1_out), .clk(GlobalClock_out), .Q(d_ff_1_q), .preset(or_1_out), .reset(MainRom_data[3]));  // open: Qn
  or or_1 (or_1_out, demultiplexer_1_out0, demultiplexer_1_out3, demultiplexer_1_out4, demultiplexer_1_out6);
  Register #(.width(3)) A (
    .D(binary_to_bcd_converter_1_p4), .en(d_ff_1_q), .clk(GlobalClock_out),
    .Q(bcd_to_7_segment_decoder_1_p1), .clr(GlobalReset_out));
  or or_2 (or_2_out, demultiplexer_1_out1, demultiplexer_1_out3, demultiplexer_1_out5, demultiplexer_1_out6);
  // _7_Segment_Display 7_segment_display_4: pin names not known; wires that end beside it: binary_to_bcd_converter_1_p4_2[3], {binary_to_bcd_converter_1_p4_2[3], binary_to_bcd_converter_1_p4}
  // BCD_to_7_Segment_decoder bcd_to_7_segment_decoder_4: pin names not known
  D_Flip_Flop d_ff_2 (
    .D(or_2_out), .clk(GlobalClock_out), .Q(d_ff_2_q), .preset(or_2_out), .reset(MainRom_data[3]));  // open: Qn
  Register #(.width(3)) B (
    .D(binary_to_bcd_converter_1_p4), .en(d_ff_2_q), .clk(GlobalClock_out),
    .Q(bcd_to_7_segment_decoder_2_p1), .clr(GlobalReset_out));
  D_Flip_Flop d_ff_3 (
    .D(demultiplexer_1_out7), .clk(GlobalClock_out), .Q(d_ff_3_q), .preset(demultiplexer_1_out7),
    .reset(or_3_out));  // open: Qn
  or or_3 (or_3_out, MainRom_data[3], GlobalReset_out);
  LedBar #(.matrixcols(9)) ledbar_1 (
    .led0(bcd_to_7_segment_decoder_1_p1[2]), .led1(bcd_to_7_segment_decoder_1_p1[1]),
    .led2(bcd_to_7_segment_decoder_1_p1[0]), .led3(bcd_to_7_segment_decoder_2_p1[2]),
    .led4(bcd_to_7_segment_decoder_2_p1[1]), .led5(bcd_to_7_segment_decoder_2_p1[0]),
    .led6(bcd_to_7_segment_decoder_3_p1[2]), .led7(bcd_to_7_segment_decoder_3_p1[1]),
    .led8(bcd_to_7_segment_decoder_3_p1[0]));
  D_Flip_Flop d_ff_4 (
    .D(or_4_out), .clk(GlobalClock_out), .Q(d_ff_4_q), .preset(or_4_out), .reset(MainRom_data[3]));  // open: Qn
  or or_4 (or_4_out, demultiplexer_1_out2, demultiplexer_1_out4, demultiplexer_1_out5, demultiplexer_1_out6);
  Register #(.width(3)) C (
    .D(binary_to_bcd_converter_1_p4), .en(d_ff_4_q), .clk(GlobalClock_out),
    .Q(bcd_to_7_segment_decoder_3_p1), .clr(GlobalReset_out));

  // Notes on the sheet:
  //   contents of MainRom (hex, n*v repeats v):
  //   0 0 8 1 9 2 a 3 8 4 9 5 a 6 8 0 9 0 a 0 f 6
endmodule
